# Fritzing sketch schema (saved by Fritzing 0.9.3b)
perfboards: 1

parts:
  Raspberry_Pi_1 = Raspberry Pi 3 [part_number=RPI-3-V1.2]
  U3 = 2-Channel 5v Relay Shield [package=relay-2ch5v10a]

nets:
  N1: Raspberry_Pi_1.GPIO3, U3.IN2
  N2: Raspberry_Pi_1.GPIO4, U3.IN1
  GND: Raspberry_Pi_1.GND, U3.GND
  5V: Raspberry_Pi_1.5V, U3.VCC

notes:
  TO 220V AC
  Audio jack to speaker+micro
  S63 connectors
  20 18 16 14 12 10 8 6 4 2
  19 17 15 13 11 9 7 5 3 1
  To cadran 1 & 2

custom parts:
  2-Channel 5v Relay Shield: 2 Channel 5v Relay Shield w. 2x SPD-06VDC-SD-C
